# Fritzing sketch wiring (saved by Fritzing 0.9.3b)
breadboards: 1

parts:
  DHT1 = DHT22 Humidity and Temperature Sensor
  Part1 = Logic Level Converter

nets:
  N1: DHT1.VDD, Part1.HV
  N2: DHT1.DATA, Part1.TX2_HV
  N3: DHT1.NULL, Part1.GND

notes:
  3.3V
  5V
  GPIO4
